# Fritzing sketch ADS1115 (saved by Fritzing 0.9.4)
breadboards: 1

parts:
  Heltec_CubeCell_Dev-Board1 = Heltec CubeCell Dev-Board [part_number=HTCC-AB01]
  Part6 = Adafruit ADS1115 16Bit I2C ADC [part_number="Adafruit #1085"]

nets:
  N1: Heltec_CubeCell_Dev-Board1.pin_11, Heltec_CubeCell_Dev-Board1.pin_14, Heltec_CubeCell_Dev-Board1.pin_18, Part6.GND
  N2: Heltec_CubeCell_Dev-Board1.pin_17, Part6.VDD
  N3: Heltec_CubeCell_Dev-Board1.pin_19, Part6.SCL
  N4: Heltec_CubeCell_Dev-Board1.pin_20, Part6.SDA

custom parts:
  Heltec CubeCell Dev-Board: CubeCell is a part of the Heltec LoRa series and incorporates an ASR6501 processor and SX1262 RF transceiver with an integrated CP2102 USB to serial port interface and onboard SHT1.25 battery interface with integrated lithium battery management system supporting direct solar panel connection.
  Adafruit ADS1115 16Bit I2C ADC: For microcontrollers without an analog-to-digital converter or when you want a higher-precision ADC, the ADS1115 provides 16-bit precision at 860 samples/second over I2C. The chip can be configured as 4 single-ended input channels, or two differential channels. As a nice bonus, it even includes a programmable gain amplifier, up to x16, to help boost up smaller single/differential signals to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
