# Fritzing sketch GY-68 (saved by Fritzing 0.9.4)
breadboards: 1

parts:
  Heltec_CubeCell_Dev-Board1 = Heltec CubeCell Dev-Board [part_number=HTCC-AB01]
  Part2 = Barometric Pressure Sensor - BMP180 Breakout (GY-68)

nets:
  N1: Heltec_CubeCell_Dev-Board1.pin_11, Heltec_CubeCell_Dev-Board1.pin_14, Heltec_CubeCell_Dev-Board1.pin_18, Part2.GND
  N2: Heltec_CubeCell_Dev-Board1.pin_17, Part2.VCC
  N3: Heltec_CubeCell_Dev-Board1.pin_19, Part2.SCL
  N4: Heltec_CubeCell_Dev-Board1.pin_20, Part2.SDA

custom parts:
  Heltec CubeCell Dev-Board: CubeCell is a part of the Heltec LoRa series and incorporates an ASR6501 processor and SX1262 RF transceiver with an integrated CP2102 USB to serial port interface and onboard SHT1.25 battery interface with integrated lithium battery management system supporting direct solar panel connection.
